# Fritzing sketch Asus_Aura_Sema (saved by Fritzing 0.9.3b)

parts:
  Parça1 = Arduino Nano (Rev3.0)
  Parça2 = Bluetooth HC-05 Macho
  J1 = Dagu DGServo 9g header (male) [package=THT]
  RGB_SMD_LED1 = SMD RGB LED (WS2812) [package=5050]  # not connected
  VCC1 = Battery block 9V

nets:
  GND: Parça1.GND, Parça2.GND, VCC1.-
  N1: Parça1.D8, J1.pulse
  N2: Parça1.D10, Parça2.TXD
  N3: Parça1.D11/MOSI, Parça2.RXD
  N4: Parça1.VIN, VCC1.+
  5V: Parça1.5V, Parça2.VCC

notes:
  Data
  GND
  12V
